// Logisim project computer.circ as structural Verilog: 8 circuits, main circuit main
module main (
);

  wire binary_to_bcd_converter_1_p2, binary_to_bcd_converter_1_p4, CARRY, clock_1_out, clock_2_out,
       clock_3_out, clock_4_out, CPC, EADD, EDIV, EIR, EMUL, EPC, ER1, ER2, ERAM, ERT, FBR1, LADD, LDIV, LIR,
       LM, LMUL, LPC, lpc_logic_1_load, LPCC, LPCCZ, LPCNZ, LPCZ, LR1, LR2, LRAM, LRO, MCR,
       n7_segment_display_4_p1, SUB, SXOR, ZERO;
  wire [3:0] IR_q_2;
  wire [7:0] multiplexer_1_out, negator_1_out, OUTR_q, ram_1_data, ram_1_data_2;
  wire [11:0] IR_q;
  wire [15:0] bit_extender_1_out, MAR_q;

  Register #(.width(16)) MAR (.D({ram_1_data_2, ram_1_data}), .en(LM), .clk(clock_1_out), .Q(MAR_q), .clr(1'b0));
  Clock clock_1 (.out(clock_1_out));
  Register OUTR (.D(ram_1_data), .en(LRO), .clk(clock_2_out), .Q(OUTR_q), .clr(1'b0));
  Clock clock_2 (.out(clock_2_out));
  lpc_logic lpc_logic_1 (
    .LPCZ(LPCZ), .ZERO(ZERO), .LPCNZ(LPCNZ), .CARRY(CARRY), .LPCCZ(LPCCZ), .LPCC(LPCC), .LPC(LPC),
    .SXOR(SXOR), .LOAD(lpc_logic_1_load));
  RAM #(.addrWidth(16), .dataWidth(16), .databus("bidir"), .\type ("nonvolatile")) ram_1 (
    .addr(MAR_q), .we(LRAM), .oe(ERAM), .clk(clock_3_out), .data({ram_1_data_2, ram_1_data}));
  Clock clock_3 (.out(clock_3_out));
  // NoConnect on ram_1_data_2
  // NoConnect on OUTR_q[6:0]
  Negator negator_1 (.in(OUTR_q), .out(negator_1_out));
  Hex_Digit_Display #(.decimalPoint("false")) hex_digit_display_1 (.value(ram_1_data_2[7:4]));
  _7_Segment_Display u_7_segment_display_1 (.g(OUTR_q[7]));  // open: f, a, b, e, d, c, dp
  _7_Segment_Display #(.decimalPoint("false")) u_7_segment_display_2 ();  // open: g, f, a, b, e, d, c
  // BCD_to_7_Segment_decoder bcd_to_7_segment_decoder_1: pin names not known
  Multiplexer #(.width(8)) multiplexer_1 (.in0(OUTR_q), .in1(negator_1_out), .out(multiplexer_1_out), .sel(OUTR_q[7]));
  // Binary_to_BCD_converter #(.binvalue(8)) binary_to_bcd_converter_1: pin names not known; wires that end beside it: multiplexer_1_out, binary_to_bcd_converter_1_p2, binary_to_bcd_converter_1_p2, binary_to_bcd_converter_1_p4
  Hex_Digit_Display #(.decimalPoint("false")) hex_digit_display_2 (.value(ram_1_data_2[3:0]));
  Hex_Digit_Display #(.decimalPoint("false")) hex_digit_display_3 (.value(ram_1_data[7:4]));
  _7_Segment_Display #(.decimalPoint("false")) u_7_segment_display_3 ();  // open: g, f, a, b, e, d, c
  // BCD_to_7_Segment_decoder bcd_to_7_segment_decoder_2: pin names not known; wires that end beside it: binary_to_bcd_converter_1_p4
  Hex_Digit_Display #(.decimalPoint("false")) hex_digit_display_4 (.value(ram_1_data[3:0]));
  pc pc_1 (
    .D_IN({ram_1_data_2, ram_1_data}), .LPC(lpc_logic_1_load), .CPC(CPC), .EPC(EPC),
    .D_OUT({ram_1_data_2, ram_1_data}));
  // _7_Segment_Display #(.decimalPoint("false")) 7_segment_display_4: pin names not known; wires that end beside it: n7_segment_display_4_p1, {ram_1_data_2, ram_1_data}
  // BCD_to_7_Segment_decoder bcd_to_7_segment_decoder_3: pin names not known; wires that end beside it: n7_segment_display_4_p1
  Register #(.width(16)) IR (
    .D({ram_1_data_2, ram_1_data}), .en(LIR), .clk(clock_4_out), .Q({IR_q_2, IR_q}), .clr(1'b0));
  Clock clock_4 (.out(clock_4_out));
  assign {ram_1_data_2, ram_1_data} = EIR ? bit_extender_1_out : 16'bz;  // Controlled_Buffer controlled_buffer_1
  assign bit_extender_1_out = {{4{1'b0}}, IR_q};  // Bit_Extender bit_extender_1
  alu alu_1 (
    .D_IN({ram_1_data_2, ram_1_data}), .EADD(EADD), .ERT(ERT), .LADD(LADD), .ER1(ER1), .SUB(SUB), .LR1(LR1),
    .EMUL(EMUL), .LMUL(LMUL), .LR2(LR2), .ER2(ER2), .EDIV(EDIV), .LDIV(LDIV),
    .D_OUT({ram_1_data_2, ram_1_data}), .CARRY(CARRY), .ZERO(ZERO), .SXOR(SXOR), .FBR1(FBR1));
  microcode microcode_1 (
    .MCR(MCR), .INS(IR_q_2), .FBR1(FBR1),
    .SIGNALS({LPCCZ, LPCNZ, LPCC, LPCZ, EDIV, LDIV, EMUL, LMUL, EADD, LADD, LR1, ER1, LR2, ER2, ERT, LIR, EIR, LPC, EPC, LM, LRAM, ERAM, MCR, CPC, LRO, SUB}));
endmodule

module alu (
  input  [15:0] D_IN,
  input  EADD,
  input  ERT,
  input  LADD,
  input  ER1,
  input  SUB,
  input  LR1,
  input  EMUL,
  input  LMUL,
  input  LR2,
  input  ER2,
  input  EDIV,
  input  LDIV,
  output [15:0] D_OUT,
  output CARRY,
  output ZERO,
  output SXOR,
  output FBR1
);

  wire alu_divider_1_fbr1, alu_multiplier_1_fbr1, CARRY_t, clock_1_out, clock_2_out, clock_3_out,
       clock_4_out, not_1_out, ZERO_t;
  wire [2:2] xor_1_out;
  wire [15:0] alu_adder_1_a_out, alu_divider_1_result, alu_multiplier_1_tr_out, controlled_buffer_1_out,
       controlled_buffer_8_out, R1T, R2T, TR_q;
  wire [31:0] controlled_buffer_5_out, controlled_buffer_6_out, controlled_buffer_7_out;

  assign controlled_buffer_1_out = ERT ? TR_q : 16'bz;  // Controlled_Buffer controlled_buffer_1
  not not_1 (not_1_out, ERT);
  assign controlled_buffer_1_out = not_1_out ? D_IN : 16'bz;  // Controlled_Buffer controlled_buffer_2
  Register #(.width(16)) R1 (.D(controlled_buffer_1_out), .en(LR1), .clk(clock_1_out), .Q(R1T), .clr(1'b0));
  Clock clock_1 (.out(clock_1_out));
  Register #(.width(16)) R2 (.D(D_IN), .en(LR2), .clk(clock_2_out), .Q(R2T), .clr(1'b0));
  Clock clock_2 (.out(clock_2_out));
  assign D_OUT = ER1 ? R1T : 16'bz;  // Controlled_Buffer controlled_buffer_3
  assign D_OUT = ER2 ? R2T : 16'bz;  // Controlled_Buffer controlled_buffer_4
  // NoConnect on R1T[14:0]
  xor xor_1 (xor_1_out[2], R1T[15], R2T[15]);
  // NoConnect on R2T[14:0]
  assign controlled_buffer_5_out = LADD ? {R2T, R1T} : 32'bz;  // Controlled_Buffer controlled_buffer_5
  assign controlled_buffer_6_out = LMUL ? {R2T, R1T} : 32'bz;  // Controlled_Buffer controlled_buffer_6
  assign controlled_buffer_7_out = LDIV ? {R2T, R1T} : 32'bz;  // Controlled_Buffer controlled_buffer_7
  Clock clock_3 (.out(clock_3_out));
  Register #(.width(3)) FLAGS (
    .D({xor_1_out[2], ZERO_t, CARRY_t}), .en(EADD), .clk(clock_3_out), .Q({SXOR, ZERO, CARRY}), .clr(1'b0));
  alu_adder alu_adder_1 (
    .A(controlled_buffer_5_out[15:0]), .B(controlled_buffer_5_out[31:16]), .SUB(SUB),
    .A_OUT(alu_adder_1_a_out), .CARRY(CARRY_t), .ZERO(ZERO_t));
  alu_multiplier alu_multiplier_1 (
    .A(controlled_buffer_6_out[15:0]), .B(controlled_buffer_6_out[31:16]), .LMUL(LMUL),
    .TR_OUT(alu_multiplier_1_tr_out), .FBR1(alu_multiplier_1_fbr1));
  alu_divider alu_divider_1 (
    .A(controlled_buffer_7_out[15:0]), .B(controlled_buffer_7_out[31:16]), .LDIV(LDIV),
    .FBR1(alu_divider_1_fbr1), .RESULT(alu_divider_1_result));
  or or_1 (FBR1, alu_multiplier_1_fbr1, alu_divider_1_fbr1);
  assign controlled_buffer_8_out = EADD ? alu_adder_1_a_out : 16'bz;  // Controlled_Buffer controlled_buffer_8
  assign controlled_buffer_8_out = EMUL ? alu_multiplier_1_tr_out : 16'bz;  // Controlled_Buffer controlled_buffer_9
  assign controlled_buffer_8_out = EDIV ? alu_divider_1_result : 16'bz;  // Controlled_Buffer controlled_buffer_10
  Register #(.width(16)) TR (.D(controlled_buffer_8_out), .en(1'b1), .clk(clock_4_out), .Q(TR_q), .clr(1'b0));
  Clock clock_4 (.out(clock_4_out));
endmodule

module microcode (
  input  MCR,
  input  [3:0] INS,
  input  FBR1,
  output [25:0] SIGNALS
);

  wire adder_1_cout, and_1_out, BR1, clock_1_out, JMP, or_1_out;
  wire [3:0] adder_1_out, MCO, multiplexer_1_out, offset_q;

  Register #(.width(4)) offset (.D(multiplexer_1_out), .en(1'b1), .clk(clock_1_out), .Q(offset_q), .clr(MCR));
  Clock clock_1 (.out(clock_1_out));
  Multiplexer #(.width(4)) multiplexer_1 (.in0(adder_1_out), .in1(MCO), .out(multiplexer_1_out), .sel(or_1_out));
  or or_1 (or_1_out, JMP, and_1_out);
  and and_1 (and_1_out, BR1, FBR1);
  Adder #(.width(4)) adder_1 (.a(offset_q), .b(4'b0001), .out(adder_1_out), .cin(1'b0), .cout(adder_1_cout));
  // NoConnect on adder_1_cout
  ROM #(.dataWidth(32)) rom_1 (.addr({INS, offset_q}), .data({BR1, JMP, MCO, SIGNALS}));
  // LedBar #(.inputtype("row"), .matrixcols(32)) ledbar_1: pin names not known; wires that end beside it: {BR1, JMP, MCO, SIGNALS}
  Hex_Digit_Display #(.decimalPoint("false")) hex_digit_display_1 (.value(MCO));

  // Notes on the sheet:
  //   contents of rom_1 (hex, n*v repeats v):
  //   c0 10 410 4 240 10 8010 8 8*0 c0 10 410 4 240 4020 8 9*0 c0 10 410 4 240 10 50 10 8010 8 6*0 c0 10
  //   410 4 240 10 50 4020 8 7*0 c0 10 410 4 240 10 2010 30000 8800 8 6*0 c0 10 410 4 240 10 2010 30001
  //   8800 8 6*0 c0 10 410 4 240 10 2010 40000 a0000000 80000 8800 8 4*0 c0 10 410 4 240 10 2010 100000
  //   a0000000 200000 8800 8 4*0 c0 10 410 4 4002 8 10*0 c0 10 410 4 240 10 2010 30001 8 7*0 c0 10 410 4
  //   300 8 10*0 c0 10 410 4 400200 8 10*0 c0 10 410 4 1000200 8 10*0 c0 10 410 4 800200 8 10*0 c0 10 410
  //   4 2000200 8 10*0 40000000
endmodule

module pc (
  input  [15:0] D_IN,
  input  LPC,
  input  CPC,
  input  EPC,
  output [15:0] D_OUT
);

  wire adder_1_cout, clock_1_out, or_1_out;
  wire [15:0] adder_1_out, controlled_buffer_1_out, PC_q;

  assign controlled_buffer_1_out = LPC ? D_IN : 16'bz;  // Controlled_Buffer controlled_buffer_1
  or or_1 (or_1_out, CPC, LPC);
  assign controlled_buffer_1_out = CPC ? adder_1_out : 16'bz;  // Controlled_Buffer controlled_buffer_2
  Register #(.width(16)) PC (.D(controlled_buffer_1_out), .en(or_1_out), .clk(clock_1_out), .Q(PC_q), .clr(1'b0));
  Clock clock_1 (.out(clock_1_out));
  Adder #(.width(16)) adder_1 (.a(16'h1), .b(PC_q), .out(adder_1_out), .cin(1'b0), .cout(adder_1_cout));
  // NoConnect on adder_1_cout
  assign D_OUT = EPC ? PC_q : 16'bz;  // Controlled_Buffer controlled_buffer_3
endmodule

module alu_multiplier (
  input  [15:0] A,
  input  [15:0] B,
  input  LMUL,
  output [15:0] TR_OUT,
  output FBR1
);

  wire adder_1_cout, clock_1_out, clock_2_out, clock_3_out, comparator_1_eq;
  wire [0:0] AR_q;
  wire [30:0] AR_q_2;
  wire [31:0] adder_1_out, bit_extender_1_out, bit_extender_2_out, BR_q, multiplexer_1_out,
       multiplexer_2_out, multiplexer_3_out, shifter_1_out, shifter_2_out;
  wire [31:16] TR_q;

  Register #(.width(32)) AR (.D(multiplexer_1_out), .en(1'b1), .clk(clock_1_out), .Q({AR_q_2, AR_q[0]}), .clr(1'b0));
  Clock clock_1 (.out(clock_1_out));
  Register #(.width(32)) BR (.D(multiplexer_2_out), .en(1'b1), .clk(clock_2_out), .Q(BR_q), .clr(1'b0));
  Clock clock_2 (.out(clock_2_out));
  Adder #(.width(32)) adder_1 (
    .a({TR_q, TR_OUT}), .b(multiplexer_3_out), .out(adder_1_out), .cin(1'b0), .cout(adder_1_cout));
  // NoConnect on adder_1_cout
  Comparator #(.width(32)) comparator_1 (.a({32{1'b0}}), .b({AR_q_2, AR_q[0]}), .eq(comparator_1_eq));  // open: gt, lt
  assign bit_extender_1_out = {{16{1'b0}}, A};  // Bit_Extender bit_extender_1
  assign bit_extender_2_out = {{16{1'b0}}, B};  // Bit_Extender bit_extender_2
  Register #(.width(32)) TR (.D(adder_1_out), .en(1'b1), .clk(clock_3_out), .Q({TR_q, TR_OUT}), .clr(LMUL));
  Clock clock_3 (.out(clock_3_out));
  not not_1 (FBR1, comparator_1_eq);
  Shifter #(.shift("lr"), .width(32)) shifter_1 (.in({AR_q_2, AR_q[0]}), .\dist (5'b00001), .out(shifter_1_out));
  Shifter #(.width(32)) shifter_2 (.in(BR_q), .\dist (5'b00001), .out(shifter_2_out));
  Multiplexer #(.width(32)) multiplexer_1 (
    .in0(shifter_1_out), .in1(bit_extender_1_out), .out(multiplexer_1_out), .sel(LMUL));
  Multiplexer #(.width(32)) multiplexer_2 (
    .in0(shifter_2_out), .in1(bit_extender_2_out), .out(multiplexer_2_out), .sel(LMUL));
  // NoConnect on TR_q
  // NoConnect on AR_q_2
  Multiplexer #(.width(32)) multiplexer_3 (.in0({32{1'b0}}), .in1(BR_q), .out(multiplexer_3_out), .sel(AR_q[0]));
endmodule

module alu_adder (
  input  [15:0] A,
  input  [15:0] B,
  input  SUB,
  output [15:0] A_OUT,
  output CARRY,
  output ZERO
);

  wire comparator_1_gt, comparator_1_lt;
  wire [15:0] multiplexer_1_out, negator_1_out;

  Negator #(.width(16)) negator_1 (.in(B), .out(negator_1_out));
  Multiplexer #(.width(16)) multiplexer_1 (.in0(B), .in1(negator_1_out), .out(multiplexer_1_out), .sel(SUB));
  Adder #(.width(16)) adder_1 (.a(A), .b(multiplexer_1_out), .out(A_OUT), .cin(1'b0), .cout(CARRY));
  // NoConnect on comparator_1_gt
  Comparator #(.width(16)) comparator_1 (
    .a(A_OUT), .b({16{1'b0}}), .gt(comparator_1_gt), .eq(ZERO), .lt(comparator_1_lt));
  // NoConnect on comparator_1_lt
endmodule

module alu_divider (
  input  [15:0] A,
  input  [15:0] B,
  input  LDIV,
  output FBR1,
  output [15:0] RESULT
);

  wire adder_1_cout, adder_2_cout, CLC, clock_1_out, clock_2_out, clock_3_out, clock_4_out, clock_5_out,
       comparator_1_eq, comparator_1_gt, comparator_1_lt, comparator_2_eq, comparator_2_gt, comparator_3_eq,
       comparator_3_gt, comparator_3_lt, comparator_4_eq, comparator_4_gt, comparator_4_lt, NEG, not_1_out,
       not_3_out, xor_1_out;
  wire [0:0] S_q;
  wire [3:0] S;
  wire [4:0] adder_1_out, multiplexer_1_out;
  wire [15:0] A_t, adder_2_out, B_t, multiplexer_2_out, multiplexer_4_out, multiplexer_5_out,
       multiplexer_6_out, multiplexer_7_out, negator_1_out, negator_2_out, negator_3_out, negator_4_out,
       or_1_out, Q_q, shifter_1_out, shifter_2_out, shifter_3_out;

  Multiplexer #(.width(5)) multiplexer_1 (.in0(adder_1_out), .in1(5'b01111), .out(multiplexer_1_out), .sel(LDIV));
  Register #(.width(16)) Q (.D(multiplexer_2_out), .en(1'b1), .clk(clock_1_out), .Q(Q_q), .clr(LDIV));
  Clock clock_1 (.out(clock_1_out));
  Shifter #(.shift("lr"), .width(16)) shifter_1 (.in(A_t), .\dist (S), .out(shifter_1_out));
  Register #(.width(5)) u_S (.D(multiplexer_1_out), .en(1'b1), .clk(clock_2_out), .Q({S, S_q[0]}), .clr(1'b0));
  Clock clock_2 (.out(clock_2_out));
  Multiplexer #(.width(16)) multiplexer_2 (.in0(or_1_out), .in1(Q_q), .out(multiplexer_2_out), .sel(not_1_out));
  // NoConnect on comparator_1_gt
  // NoConnect on comparator_1_eq
  Comparator #(.width(16)) comparator_1 (
    .a(shifter_1_out), .b(B_t), .gt(comparator_1_gt), .eq(comparator_1_eq), .lt(comparator_1_lt));
  not not_1 (not_1_out, CLC);
  Negator #(.width(16)) negator_1 (.in(Q_q), .out(negator_1_out));
  not not_2 (CLC, comparator_1_lt);
  // NoConnect on comparator_2_gt
  // NoConnect on comparator_2_eq
  Comparator #(.width(5)) comparator_2 (
    .a({5{1'b0}}), .b({S, S_q[0]}), .gt(comparator_2_gt), .eq(comparator_2_eq), .lt(FBR1));
  // NoConnect on comparator_3_gt
  // NoConnect on comparator_3_eq
  Comparator #(.width(16)) comparator_3 (
    .a(A), .b({16{1'b0}}), .gt(comparator_3_gt), .eq(comparator_3_eq), .lt(comparator_3_lt));
  // NoConnect on comparator_4_gt
  // NoConnect on comparator_4_eq
  Comparator #(.width(16)) comparator_4 (
    .a(B), .b({16{1'b0}}), .gt(comparator_4_gt), .eq(comparator_4_eq), .lt(comparator_4_lt));
  Negator #(.width(16)) negator_2 (.in(B), .out(negator_2_out));
  assign or_1_out = Q_q | shifter_2_out;  // OR_Gate or_1, 16 bits wide
  Shifter #(.width(16)) shifter_2 (.in(16'h1), .\dist (S), .out(shifter_2_out));
  Multiplexer #(.width(16)) multiplexer_3 (.in0(Q_q), .in1(negator_1_out), .out(RESULT), .sel(NEG));
  Adder #(.width(5)) adder_1 (.a({5{1'b1}}), .b({S, S_q[0]}), .out(adder_1_out), .cin(1'b0), .cout(adder_1_cout));
  // NoConnect on adder_1_cout
  // NoConnect on S_q[0]
  Negator #(.width(16)) negator_3 (.in(A), .out(negator_3_out));
  Multiplexer #(.width(16)) multiplexer_4 (
    .in0(B), .in1(negator_2_out), .out(multiplexer_4_out), .sel(comparator_4_lt));
  Multiplexer #(.width(16)) multiplexer_5 (
    .in0(A), .in1(negator_3_out), .out(multiplexer_5_out), .sel(comparator_3_lt));
  Register #(.width(1)) u_NEG (.D(xor_1_out), .en(LDIV), .clk(clock_3_out), .Q(NEG), .clr(1'b0));
  xor xor_1 (xor_1_out, comparator_3_lt, comparator_4_lt);
  Clock clock_3 (.out(clock_3_out));
  Multiplexer #(.width(16)) multiplexer_6 (
    .in0(multiplexer_5_out), .in1(multiplexer_7_out), .out(multiplexer_6_out), .sel(not_3_out));
  not not_3 (not_3_out, LDIV);
  Register #(.width(16)) AR (.D(multiplexer_6_out), .en(1'b1), .clk(clock_4_out), .Q(A_t), .clr(1'b0));
  Clock clock_4 (.out(clock_4_out));
  Shifter #(.width(16)) shifter_3 (.in(B_t), .\dist (S), .out(shifter_3_out));
  Negator #(.width(16)) negator_4 (.in(shifter_3_out), .out(negator_4_out));
  Register #(.width(16)) BR (.D(multiplexer_4_out), .en(LDIV), .clk(clock_5_out), .Q(B_t), .clr(1'b0));
  Clock clock_5 (.out(clock_5_out));
  Multiplexer #(.width(16)) multiplexer_7 (.in0(A_t), .in1(adder_2_out), .out(multiplexer_7_out), .sel(CLC));
  Adder #(.width(16)) adder_2 (.a(A_t), .b(negator_4_out), .out(adder_2_out), .cin(1'b0), .cout(adder_2_cout));
  // NoConnect on adder_2_cout
endmodule

module lpc_logic (
  input  LPCZ,
  input  ZERO,
  input  LPCNZ,
  input  CARRY,
  input  LPCCZ,
  input  LPCC,
  input  LPC,
  input  SXOR,
  output LOAD
);

  wire and_1_out, and_2_out, and_3_out, and_4_out, and_5_out, multiplexer_1_out, multiplexer_2_out,
       not_1_out, not_2_out, not_3_out, not_4_out, not_5_out, not_6_out, xor_1_out;

  xor xor_1 (xor_1_out, LPCC, LPCCZ);
  and and_1 (and_1_out, LPCC, CARRY, not_1_out);
  not not_1 (not_1_out, ZERO);
  not not_2 (not_2_out, ZERO);
  not not_3 (not_3_out, CARRY);
  and and_2 (and_2_out, not_2_out, not_3_out, LPCCZ);
  not not_4 (not_4_out, and_1_out);
  and and_3 (and_3_out, SXOR, xor_1_out);
  not not_5 (not_5_out, and_2_out);
  not not_6 (not_6_out, ZERO);
  Multiplexer multiplexer_1 (.in0(and_1_out), .in1(not_4_out), .out(multiplexer_1_out), .sel(and_3_out));
  Multiplexer multiplexer_2 (.in0(and_2_out), .in1(not_5_out), .out(multiplexer_2_out), .sel(and_3_out));
  and and_4 (and_4_out, LPCZ, ZERO);
  and and_5 (and_5_out, LPCNZ, not_6_out);
  or or_1 (LOAD, and_4_out, and_5_out, multiplexer_1_out, multiplexer_2_out, LPC);
endmodule
